# Fritzing sketch am2302 (saved by Fritzing 0.9.3b)
circuit board: 8.46667cm x 5.64444cm
breadboards: 1

parts:
  DHT1 = DHT22 Humidity and Temperature Sensor
  Composant1 = Arduino Uno (Rev3)
  R1 = Resistor [tolerance=±5% resistance=10k package=THT]

nets:
  VDD: DHT1.VDD, Composant1.5V, R1.Pin_1
  N1: DHT1.DATA, Composant1.D2, R1.Pin_0
  GND: DHT1.GND, Composant1.GND
